# Fritzing sketch Montaje1 (saved by Fritzing 0.9.3b)
breadboards: 1

parts:
  Arduino = Arduino Uno (Rev3) - ICSP
  Modulo_DHT11 = DHT11 module

nets:
  GND: Arduino.GND, Modulo_DHT11.GND
  N1: Arduino.D2, Modulo_DHT11.DATA
  5V: Arduino.5V, Modulo_DHT11.VCC

custom parts:
  DHT11 module: DHT11 black pcb module
